# Fritzing sketch counter_board (saved by Fritzing 0.9.3b)
breadboards: 1

parts:
  R1 = Resistor [tolerance=±5% resistance=4.7k package=THT]
  U1 = attiny85 [package=dip]
  R2 = Resistor [tolerance=±5% resistance=4.7k package=THT]
  R5 = Resistor [tolerance=±5% resistance=220 package=THT]
  U2 = TLP621 [package=THT]
  U3 = TLP621 [package=THT]
  R6 = Resistor [tolerance=±5% resistance=220 package=THT]
  R7 = Resistor [tolerance=±5% resistance=220 package=THT]
  R8 = Resistor [tolerance=±5% resistance=220 package=THT]
  R9 = Resistor [tolerance=±5% resistance=220 package=THT]
  D3 = Zener Diode [part_number=1N4732A breakdown_voltage=3.6V package="300 mil [THT]"]
  C1 = Ceramic Capacitor [capacitance=100nF package="100 mil [THT, multilayer]"]
  Q1 = MOSFET-NCHANNEL [package=to220v]
  U4 = atmega328 [package=dip]
  speed_sensor_signal_(-) = Header 1 [package=smtso-256-et]
  R11 = Resistor [tolerance=±5% resistance=220 package="2010 [SMD]"]
  +12v = Header 1 [package=smtso-256-et]
  +12v_2 = Header 1 [package=smtso-256-et]
  tacho_sensor_signal_(-) = Header 1 [package=smtso-256-et]
  R12 = Resistor [tolerance=±5% resistance=220 package="2010 [SMD]"]
  display_(spi) = Header 1 [package=smtso-256-et]
  display_(spi)_2 = Header 1 [package=smtso-256-et]
  display_(spi)_3 = Header 1 [package=smtso-256-et]
  display_(spi)_4 = Header 1 [package=smtso-256-et]
  display_(GND) = Header 1 [package=smtso-256-et]
  display_(VCC) = Header 1 [package=smtso-256-et]
  U5 = Voltage Regulator - 5V [package="TO220 [THT]"]
  VCC_(12v_ignition) = Header 1 [package=smtso-256-et]
  GND = Header 1 [package=smtso-256-et]

nets (from the schematic view):
  N1: R1.Pin_0, U1.Pin_8, R2.Pin_0, U2.Pin_4, U3.Pin_4, R11.Pin_1
  N2: R1.Pin_1, U1.Pin_7, U4.A5
  N3: U1.Pin_1, R11.Pin_0
  N4: U1.Pin_2, U2.Pin_3, R6.Pin_0
  N5: U1.Pin_3, U3.Pin_3, R7.Pin_0
  GND: U1.Pin_4, R6.Pin_1, R7.Pin_1, U4.GND, display_(GND).1, U5.GND, GND.1
  N6: U1.Pin_5, R2.Pin_1, U4.A4
  N7: R5.Pin_0, speed_sensor_signal_(-).1
  N8: R5.Pin_1, U2.Pin_2
  N9: U2.Pin_1, +12v.1
  N10: U3.Pin_1, Q1.D, +12v_2.1
  N11: U3.Pin_2, D3.anode, C1.0, Q1.S
  N12: R8.Pin_0, tacho_sensor_signal_(-).1
  N13: R8.Pin_1, R9.Pin_0, D3.cathode
  N14: R9.Pin_1, C1.1, Q1.G
  N15: U4.RESET, R12.Pin_1
  N16: U4.VCC, U4.AVCC, R12.Pin_0, display_(VCC).1, U5.output_voltage
  N17: U4.D10_(PWM), display_(spi)_4.1
  N18: U4.D11_(PWM), display_(spi)_3.1
  N19: U4.D12, display_(spi)_2.1
  N20: U4.D13, display_(spi).1
  N21: U5.input_voltage, VCC_(12v_ignition).1
